// Logisim project cerrojo_logica.circ as structural Verilog: 10 circuits, main circuit main
module main (
  input  Dedo1,
  input  Dedo2,
  input  Dedo3,
  input  Dedo4
);

  wire CLK_out, codificador_dedos_1_d0, codificador_dedos_1_d1, codificador_dedos_1_d2,
       contador_digitos_1_listo, decodificador_anuncios_1_a, decodificador_anuncios_1_b,
       decodificador_anuncios_1_c, decodificador_anuncios_1_d, decodificador_anuncios_1_e,
       decodificador_anuncios_1_f, decodificador_anuncios_1_g, decodificador_claves_1_abrir,
       decodificador_claves_1_cerrar, latch_sr_1_abrirlatch, latch_sr_1_cerrarlatch,
       registro_desplazamiento_9bits_1_p0, registro_desplazamiento_9bits_1_p1,
       registro_desplazamiento_9bits_1_p2, registro_desplazamiento_9bits_1_p3,
       registro_desplazamiento_9bits_1_p4, registro_desplazamiento_9bits_1_p5,
       registro_desplazamiento_9bits_1_p6, registro_desplazamiento_9bits_1_p7,
       registro_desplazamiento_9bits_1_p8, Reset_out, serializador_mux_1_fin_digito,
       serializador_mux_1_linea_serial;

  Button CLK (.out(CLK_out));
  Button Reset (.out(Reset_out));
  Codificador_Dedos codificador_dedos_1 (
    .Dedo1(Dedo1), .Dedo2(Dedo2), .Dedo3(Dedo3), .Dedo4(Dedo4), .D2(codificador_dedos_1_d2),
    .D1(codificador_dedos_1_d1), .D0(codificador_dedos_1_d0));
  Serializador_MUX serializador_mux_1 (
    .D2(codificador_dedos_1_d2), .D1(codificador_dedos_1_d1), .D0(codificador_dedos_1_d0), .CLK(CLK_out),
    .Reset(Reset_out), .Linea_Serial(serializador_mux_1_linea_serial),
    .Fin_Digito(serializador_mux_1_fin_digito));
  Registro_Desplazamiento_9bits registro_desplazamiento_9bits_1 (
    .Dato_Serial(serializador_mux_1_linea_serial), .CLK(CLK_out), .Reset(Reset_out),
    .P0(registro_desplazamiento_9bits_1_p0), .P1(registro_desplazamiento_9bits_1_p1),
    .P2(registro_desplazamiento_9bits_1_p2), .P3(registro_desplazamiento_9bits_1_p3),
    .P4(registro_desplazamiento_9bits_1_p4), .P5(registro_desplazamiento_9bits_1_p5),
    .P6(registro_desplazamiento_9bits_1_p6), .P7(registro_desplazamiento_9bits_1_p7),
    .P8(registro_desplazamiento_9bits_1_p8));
  Contador_Digitos contador_digitos_1 (
    .Fin_Digito(serializador_mux_1_fin_digito), .Reset(Reset_out), .Listo(contador_digitos_1_listo));
  Decodificador_Claves decodificador_claves_1 (
    .P0(registro_desplazamiento_9bits_1_p0), .P1(registro_desplazamiento_9bits_1_p1),
    .P2(registro_desplazamiento_9bits_1_p2), .P3(registro_desplazamiento_9bits_1_p3),
    .P4(registro_desplazamiento_9bits_1_p4), .P5(registro_desplazamiento_9bits_1_p5),
    .P6(registro_desplazamiento_9bits_1_p6), .P7(registro_desplazamiento_9bits_1_p7),
    .P8(registro_desplazamiento_9bits_1_p8), .Abrir(decodificador_claves_1_abrir),
    .Cerrar(decodificador_claves_1_cerrar));
  LED led_1 (.in(latch_sr_1_abrirlatch));
  Latch_SR latch_sr_1 (
    .Abrir(decodificador_claves_1_abrir), .Cerrar(decodificador_claves_1_cerrar),
    .AbrirLatch(latch_sr_1_abrirlatch), .CerrarLatch(latch_sr_1_cerrarlatch));
  LED led_2 (.in(latch_sr_1_cerrarlatch));
  Decodificador_Anuncios decodificador_anuncios_1 (
    .Abrir(decodificador_claves_1_abrir), .Cerrar(decodificador_claves_1_cerrar),
    .Listo(contador_digitos_1_listo), .a(decodificador_anuncios_1_a), .b(decodificador_anuncios_1_b),
    .c(decodificador_anuncios_1_c), .d(decodificador_anuncios_1_d), .e(decodificador_anuncios_1_e),
    .f(decodificador_anuncios_1_f), .g(decodificador_anuncios_1_g));
  _7_Segment_Display u_7_segment_display_1 (
    .g(decodificador_anuncios_1_g), .f(decodificador_anuncios_1_f), .a(decodificador_anuncios_1_a),
    .b(decodificador_anuncios_1_b), .e(decodificador_anuncios_1_e), .d(decodificador_anuncios_1_d),
    .c(decodificador_anuncios_1_c));  // open: dp
endmodule

module Decodificador_Claves (
  input  P0,
  input  P1,
  input  P2,
  input  P3,
  input  P4,
  input  P5,
  input  P6,
  input  P7,
  input  P8,
  output Abrir,
  output Cerrar
);

  wire and_1_out, and_2_out, and_3_out, nor_1_out, nor_2_out, nor_3_out, nor_4_out, not_1_out, not_2_out;

  nor nor_1 (nor_1_out, P0, P5);
  not not_1 (not_1_out, P7);
  nor nor_2 (nor_2_out, P1, P4);
  nor nor_3 (nor_3_out, not_1_out, P8);
  not not_2 (not_2_out, P6);
  nor nor_4 (nor_4_out, P3, P2);
  and and_1 (and_1_out, nor_2_out, nor_3_out);
  and and_2 (and_2_out, not_2_out, nor_4_out);
  and and_3 (and_3_out, nor_1_out, P2, P3, P6);
  and and_4 (Abrir, and_3_out, and_1_out);
  and and_5 (Cerrar, and_1_out, and_2_out, P5, P0);

  // Notes on the sheet:
  //   COMUN
endmodule

module Decodificador_Abrir (
  input  P0,
  input  P1,
  input  P2,
  input  P3,
  input  P4,
  input  P5,
  input  P6,
  input  P7,
  input  P8,
  output Abrir
);

  wire not_1_out, not_2_out, not_3_out, not_4_out, not_5_out;

  not not_1 (not_1_out, P0);
  not not_2 (not_2_out, P1);
  not not_3 (not_3_out, P4);
  not not_4 (not_4_out, P5);
  not not_5 (not_5_out, P8);
  and and_1 (Abrir, not_1_out, not_2_out, P2, P3, not_3_out, not_4_out, P6, P7, not_5_out);
endmodule

module Decodificador_Cerrar (
  input  P0,
  input  P1,
  input  P2,
  input  P3,
  input  P4,
  input  P5,
  input  P6,
  input  P7,
  input  P8,
  output Cerrar
);

  wire not_1_out, not_2_out, not_3_out, not_4_out, not_5_out, not_6_out;

  not not_1 (not_1_out, P1);
  not not_2 (not_2_out, P2);
  not not_3 (not_3_out, P3);
  not not_4 (not_4_out, P4);
  not not_5 (not_5_out, P6);
  not not_6 (not_6_out, P8);
  and and_1 (Cerrar, P0, not_1_out, not_2_out, not_3_out, not_4_out, P5, not_5_out, P7, not_6_out);
endmodule

module Latch_SR (
  input  Abrir,
  input  Cerrar,
  output AbrirLatch,
  output CerrarLatch
);

  nor nor_1 (CerrarLatch, Abrir, AbrirLatch);
  nor nor_2 (AbrirLatch, CerrarLatch, Cerrar);
endmodule

module Decodificador_Anuncios (
  input  Abrir,
  input  Cerrar,
  input  Listo,
  output a,
  output b,
  output c,
  output d,
  output e,
  output f,
  output g
);

  wire nor_1_out, or_2_out, S_C_out, S_E_out;

  nor nor_1 (nor_1_out, Cerrar, Abrir);
  and S_A (b, Listo, Abrir);
  and S_C (S_C_out, Cerrar, Listo);
  and S_E (S_E_out, Listo, nor_1_out);
  not not_1 (d, b);
  or or_1 (g, S_E_out, b);
  or or_2 (or_2_out, S_E_out, S_C_out);
  or or_3 (a, or_2_out, b);

  assign c = b;
  assign e = 1'b1;
  assign f = 1'b1;
endmodule

module Codificador_Dedos (
  input  Dedo1,
  input  Dedo2,
  input  Dedo3,
  input  Dedo4,
  output D2,
  output D1,
  output D0
);

  wire not_1_out, xor_1_out, xor_2_out;

  not not_1 (not_1_out, Dedo4);
  xor xor_1 (xor_1_out, Dedo4, Dedo3);
  xor xor_2 (xor_2_out, Dedo2, Dedo1);
  and and_1 (D2, Dedo1, Dedo2, Dedo3, Dedo4);
  and and_2 (D1, Dedo2, not_1_out);
  xor xor_3 (D0, xor_1_out, xor_2_out);
endmodule

module Serializador_MUX (
  input  D2,
  input  D1,
  input  D0,
  input  CLK,
  input  Reset,
  output Linea_Serial,
  output Fin_Digito
);

  wire and_1_out, d_ff_1_q, d_ff_2_q, d_ff_2_qn, n74153_1_pin1, n74153_1_pin15;

  D_Flip_Flop d_ff_1 (.D(Fin_Digito), .clk(CLK), .Q(d_ff_1_q), .reset(Reset));  // open: Qn, preset
  D_Flip_Flop d_ff_2 (.D(and_1_out), .clk(CLK), .Q(d_ff_2_q), .Qn(d_ff_2_qn), .reset(Reset));  // open: preset
  _74153 u_74153_1 (
    .pin1(n74153_1_pin1), .pin2(d_ff_1_q), .pin3(n74153_1_pin1), .pin4(D1), .pin5(D2), .pin6(D0),
    .pin7(Linea_Serial), .pin15(n74153_1_pin15), .pin14(d_ff_2_q));  // open: pin13, pin12, pin11, pin10, pin9
  nor nor_1 (Fin_Digito, d_ff_1_q, d_ff_2_q);
  and and_1 (and_1_out, d_ff_1_q, d_ff_2_qn);
  // also tied to GND on the sheet: n74153_1_pin1
  // also tied to VCC on the sheet: n74153_1_pin15
endmodule

module Registro_Desplazamiento_9bits (
  input  Dato_Serial,
  input  CLK,
  input  Reset,
  output P0,
  output P1,
  output P2,
  output P3,
  output P4,
  output P5,
  output P6,
  output P7,
  output P8
);

  // Shift_Register #(.length(9)) shift_register_1: pin names not known; wires that end beside it: Reset, 1'b0, 1'b1, CLK, Dato_Serial, P8, P7, P6, P5, P4, P3, P2, P1, P0

  // Notes on the sheet:
  //   Pequeño error de cálculo :(
endmodule

module Contador_Digitos (
  input  Fin_Digito,
  input  Reset,
  output Listo
);

  wire d_ff_1_qn, d_ff_2_q;

  D_Flip_Flop d_ff_1 (.D(d_ff_2_q), .clk(Fin_Digito), .Qn(d_ff_1_qn), .reset(Reset));  // open: Q, preset
  D_Flip_Flop d_ff_2 (.D(d_ff_1_qn), .clk(Fin_Digito), .Q(d_ff_2_q), .reset(Reset));  // open: Qn, preset
  nor nor_1 (Listo, d_ff_1_qn, d_ff_2_q);
endmodule
